// Logisim project Mon premier cpu.circ as structural Verilog: 3 circuits, main circuit main
module main (
  input  Start,
  input  [31:0] in_2,
  output [2:0] Value_B,
  output [2:0] value_A,
  output Jump_to_0,
  output [2:0] ALU_code,
  output [2:0] Ram_address,
  output [2:0] What_write,
  output Reset_clear_ram,
  output Read_ram,
  output [3:0] Jump_to
);

  wire and_1_out, clock_1_out, decoder_2_jump_to_0, decoder_2_read_ram, decoder_2_reset_ram, not_1_out,
       or_1_out, or_2_out, or_3_out, or_4_out, or_5_out;
  wire [2:0] adder_2_out, decoder_2_address_of_value_a, decoder_2_adress_of_value_b, decoder_2_alu_code,
       decoder_2_ram_address, decoder_2_what_write, or_6_out;
  wire [3:0] adder_1_out, bit_extender_1_out, decoder_2_jump_rom, multiplexer_1_out, register_1_q;
  wire [31:0] rom_1_data;

  Adder #(.width(4)) adder_1 (.a(register_1_q), .b(bit_extender_1_out), .out(adder_1_out));  // open: cin, cout
  assign bit_extender_1_out = {{3{1'b0}}, Start};  // Bit_Extender bit_extender_1
  not not_1 (not_1_out, Start);
  Clock clock_1 (.out(clock_1_out));
  or or_1 (or_1_out, decoder_2_alu_code[0], decoder_2_alu_code[1], decoder_2_alu_code[2]);
  Multiplexer #(.width(4), .enable("false")) multiplexer_1 (
    .in0(adder_1_out), .in1(decoder_2_jump_rom), .out(multiplexer_1_out), .sel(or_2_out));
  and and_1 (and_1_out, clock_1_out, Start);
  Bit_Extender #(.in_width(1), .out_width(3)) bit_extender_2 (.in(or_1_out));  // open: out
  or or_2 (or_2_out, decoder_2_jump_rom[0], decoder_2_jump_rom[1], decoder_2_jump_rom[2], decoder_2_jump_rom[3], or_3_out);
  or or_3 (or_3_out, decoder_2_jump_to_0, not_1_out);
  Register #(.width(4)) register_1 (.D(multiplexer_1_out), .Q(register_1_q), .clk(and_1_out));  // open: en, clr
  Adder #(.width(3)) adder_2 (
    .a(decoder_2_address_of_value_a), .b(decoder_2_adress_of_value_b), .out(adder_2_out));  // open: cin, cout
  // Probe on in_2
  decoder decoder_1 (
    .in_1(in_2), .address_of_value_A(Value_B), .Adress_of_value_B(value_A), .ALU_code(ALU_code),
    .Ram_address(Ram_address), .What_write(What_write), .Reset_ram(Reset_clear_ram), .Read_ram(Read_ram),
    .Jump_rom(Jump_to), .Jump_to_0(Jump_to_0));
  ROM #(.addrWidth(4), .dataWidth(32)) rom_1 (.addr(register_1_q), .data(rom_1_data));  // open: sel
  or or_4 (or_4_out, adder_2_out[0], adder_2_out[1], adder_2_out[2]);
  decoder decoder_2 (
    .in_1(rom_1_data), .address_of_value_A(decoder_2_address_of_value_a),
    .Adress_of_value_B(decoder_2_adress_of_value_b), .ALU_code(decoder_2_alu_code),
    .Ram_address(decoder_2_ram_address), .What_write(decoder_2_what_write), .Reset_ram(decoder_2_reset_ram),
    .Read_ram(decoder_2_read_ram), .Jump_rom(decoder_2_jump_rom), .Jump_to_0(decoder_2_jump_to_0));
  or or_5 (or_5_out, decoder_2_what_write[0], decoder_2_what_write[1], decoder_2_what_write[2], or_4_out);
  assign or_6_out = decoder_2_what_write | adder_2_out;  // OR_Gate or_6, 3 bits wide
  RAM #(.addrWidth(3), .dataWidth(3), .bus("separate")) ram_1 (
    .addr(decoder_2_ram_address), .din(or_6_out), .str(or_5_out), .clk(or_5_out), .ld(decoder_2_read_ram),
    .clr(decoder_2_reset_ram));  // open: data, sel

  // Notes on the sheet:
  //   Program creator
  //   contents of rom_1 (hex, n*v repeats v):
  //   4000000 e0000000
endmodule

module decoder (
  input  [31:0] in_1,
  output [2:0] address_of_value_A,
  output [2:0] Adress_of_value_B,
  output [2:0] ALU_code,
  output [2:0] Ram_address,
  output [2:0] What_write,
  output Reset_ram,
  output Read_ram,
  output [3:0] Jump_rom,
  output Jump_to_0
);

  wire [31:0] pull_resistor_1_node;

  Pull_Resistor pull_resistor_1 (.node(pull_resistor_1_node));
  Comparator #(.width(32)) comparator_1 (.a(in_1), .b(pull_resistor_1_node), .eq(Jump_to_0));  // open: gt, lt

  assign address_of_value_A = in_1[13:11];
  assign Adress_of_value_B = in_1[16:14];
  assign ALU_code = in_1[19:17];
  assign Jump_rom = in_1[31:28];
  assign Ram_address = in_1[22:20];
  assign Read_ram = in_1[27];
  assign Reset_ram = in_1[26];
  assign What_write = in_1[25:23];
endmodule

module delay (
  input  [2:0] in_1,
  output [2:0] out_2
);

  wire [2:0] buffer_1_out, buffer_2_out, buffer_3_out, buffer_4_out, buffer_5_out, buffer_6_out,
       buffer_7_out, buffer_8_out, buffer_9_out, buffer_10_out, buffer_11_out, buffer_12_out, buffer_13_out,
       buffer_14_out, buffer_15_out, buffer_16_out, buffer_17_out, buffer_18_out, buffer_19_out,
       buffer_20_out, buffer_21_out, buffer_22_out, buffer_23_out, buffer_24_out, buffer_25_out,
       buffer_26_out, buffer_27_out, buffer_28_out, buffer_29_out, buffer_30_out, buffer_31_out,
       buffer_32_out, buffer_33_out, buffer_34_out, buffer_35_out, buffer_36_out, buffer_37_out,
       buffer_38_out, buffer_39_out, buffer_40_out, buffer_41_out, buffer_42_out, buffer_43_out;

  assign buffer_1_out = buffer_2_out;  // Buffer buffer_1, 3 bits wide
  assign buffer_2_out = in_1;  // Buffer buffer_2, 3 bits wide
  assign buffer_3_out = buffer_5_out;  // Buffer buffer_3, 3 bits wide
  assign buffer_4_out = buffer_6_out;  // Buffer buffer_4, 3 bits wide
  assign buffer_5_out = buffer_4_out;  // Buffer buffer_5, 3 bits wide
  assign buffer_6_out = buffer_1_out;  // Buffer buffer_6, 3 bits wide
  assign buffer_7_out = buffer_9_out;  // Buffer buffer_7, 3 bits wide
  assign buffer_8_out = buffer_7_out;  // Buffer buffer_8, 3 bits wide
  assign buffer_9_out = buffer_10_out;  // Buffer buffer_9, 3 bits wide
  assign buffer_10_out = buffer_3_out;  // Buffer buffer_10, 3 bits wide
  assign buffer_11_out = buffer_13_out;  // Buffer buffer_11, 3 bits wide
  assign buffer_12_out = buffer_14_out;  // Buffer buffer_12, 3 bits wide
  assign buffer_13_out = buffer_12_out;  // Buffer buffer_13, 3 bits wide
  assign buffer_14_out = buffer_8_out;  // Buffer buffer_14, 3 bits wide
  assign buffer_15_out = buffer_17_out;  // Buffer buffer_15, 3 bits wide
  assign buffer_16_out = buffer_18_out;  // Buffer buffer_16, 3 bits wide
  assign buffer_17_out = buffer_16_out;  // Buffer buffer_17, 3 bits wide
  assign buffer_18_out = buffer_11_out;  // Buffer buffer_18, 3 bits wide
  assign buffer_19_out = buffer_21_out;  // Buffer buffer_19, 3 bits wide
  assign buffer_20_out = buffer_19_out;  // Buffer buffer_20, 3 bits wide
  assign buffer_21_out = buffer_22_out;  // Buffer buffer_21, 3 bits wide
  assign buffer_22_out = buffer_15_out;  // Buffer buffer_22, 3 bits wide
  assign buffer_23_out = buffer_26_out;  // Buffer buffer_23, 3 bits wide
  assign buffer_24_out = buffer_23_out;  // Buffer buffer_24, 3 bits wide
  assign buffer_25_out = buffer_20_out;  // Buffer buffer_25, 3 bits wide
  assign buffer_26_out = buffer_25_out;  // Buffer buffer_26, 3 bits wide
  assign buffer_27_out = buffer_29_out;  // Buffer buffer_27, 3 bits wide
  assign buffer_28_out = buffer_27_out;  // Buffer buffer_28, 3 bits wide
  assign buffer_29_out = buffer_24_out;  // Buffer buffer_29, 3 bits wide
  assign buffer_30_out = buffer_28_out;  // Buffer buffer_30, 3 bits wide
  assign buffer_31_out = buffer_33_out;  // Buffer buffer_31, 3 bits wide
  assign buffer_32_out = buffer_31_out;  // Buffer buffer_32, 3 bits wide
  assign buffer_33_out = buffer_34_out;  // Buffer buffer_33, 3 bits wide
  assign buffer_34_out = buffer_30_out;  // Buffer buffer_34, 3 bits wide
  assign buffer_35_out = buffer_32_out;  // Buffer buffer_35, 3 bits wide
  assign buffer_36_out = buffer_35_out;  // Buffer buffer_36, 3 bits wide
  assign buffer_37_out = buffer_38_out;  // Buffer buffer_37, 3 bits wide
  assign buffer_38_out = buffer_36_out;  // Buffer buffer_38, 3 bits wide
  assign buffer_39_out = buffer_41_out;  // Buffer buffer_39, 3 bits wide
  assign buffer_40_out = buffer_37_out;  // Buffer buffer_40, 3 bits wide
  assign buffer_41_out = buffer_40_out;  // Buffer buffer_41, 3 bits wide
  assign buffer_42_out = buffer_39_out;  // Buffer buffer_42, 3 bits wide
  assign buffer_43_out = buffer_42_out;  // Buffer buffer_43, 3 bits wide
  assign out_2 = buffer_43_out;  // Buffer buffer_44, 3 bits wide
endmodule
