// Logisim project mon premier cpu v2.circ as structural Verilog: 7 circuits, main circuit main
module main (
  input  Start,
  input  [2:0] Value_B,
  input  [2:0] value_A,
  input  [2:0] ALU_code,
  input  [2:0] Ram_address,
  input  [7:0] What_write,
  input  Reset_clear_ram,
  input  [3:0] Jump_to,
  output [1:0] Select_code,
  output [7:0] Loaded_value,
  output [7:0] out_11,
  output [31:0] out_12
);

  wire alu_1_overflow_plus, and_1_out, clock_1_out, clock_2_out, decoder_1_jump_to_0, decoder_1_reset_ram,
       not_1_out, not_2_out, not_3_out, not_4_out, not_5_out, or_5_out, test_0_1_out_2, test_0_2_out_2,
       test_0_3_out_2, test_0_4_out_2, test_0_5_out_2;
  wire [2:0] decoder_1_address_of_value_a, decoder_1_adress_of_value_b, decoder_1_alu_code,
       decoder_1_ram_address, or_2_out;
  wire [3:0] decoder_1_jump_rom, instruction_counter_1_out_5;
  wire [7:0] alu_1_out_4, decoder_1_what_write, multiplexer_1_out, or_4_out, pull_resistor_2_node,
       register_1_q, register_2_q, register_3_q;
  wire [31:0] rom_1_data;

  Register register_1 (.D(multiplexer_1_out), .Q(register_1_q), .clk(not_2_out));  // open: en, clr
  Clock clock_1 (.out(clock_1_out));
  Register register_2 (.D(out_11), .Q(register_2_q), .clk(not_3_out));  // open: en, clr
  Instruction_counter instruction_counter_1 (
    .Cycles(clock_1_out), .Start(Start), .Jump_to(decoder_1_jump_rom), .Jump_to_0(decoder_1_jump_to_0),
    .out_5(instruction_counter_1_out_5));
  Multiplexer #(.width(8), .enable("false")) multiplexer_1 (
    .in0(pull_resistor_2_node), .in1({8{1'b0}}), .out(multiplexer_1_out), .sel(alu_1_overflow_plus));
  ALU alu_1 (
    .value_A(register_1_q), .value_B(register_2_q), .out_4(alu_1_out_4), .ALU_code(decoder_1_alu_code),
    .Overflow_plus(alu_1_overflow_plus));  // open: a_b, a__b, a_b_2, Overflow_minus, Overflow_star
  coder coder_1 (
    .out_8(out_12), .address_of_value_A(Value_B), .Adress_of_value_B(value_A), .ALU_code(ALU_code),
    .Ram_address(Ram_address), .What_write(What_write), .Reset_ram(Reset_clear_ram), .Jump_rom(Jump_to));
  // Probe on out_12
  ROM #(.addrWidth(4), .dataWidth(32)) rom_1 (.addr(instruction_counter_1_out_5), .data(rom_1_data));  // open: sel
  test_0 test_0_1 (.in_1(alu_1_out_4), .out_2(test_0_1_out_2));
  Pull_Resistor pull_resistor_1 (.node(alu_1_out_4));
  decoder decoder_1 (
    .in_1(rom_1_data), .address_of_value_A(decoder_1_address_of_value_a),
    .Adress_of_value_B(decoder_1_adress_of_value_b), .ALU_code(decoder_1_alu_code),
    .Ram_address(decoder_1_ram_address), .What_write(decoder_1_what_write), .Reset_ram(decoder_1_reset_ram),
    .Jump_rom(decoder_1_jump_rom), .Jump_to_0(decoder_1_jump_to_0));
  not not_1 (not_1_out, test_0_1_out_2);
  not not_2 (not_2_out, test_0_2_out_2);
  test_0 test_0_2 (.in_1(pull_resistor_2_node), .out_2(test_0_2_out_2));
  not not_3 (not_3_out, test_0_3_out_2);
  test_0 test_0_3 (.in_1(out_11), .out_2(test_0_3_out_2));
  or or_1 (Select_code[0], decoder_1_address_of_value_a[2], decoder_1_address_of_value_a[1], decoder_1_address_of_value_a[0]);
  Register register_3 (.D(alu_1_out_4), .Q(register_3_q), .clk(not_4_out));  // open: en, clr
  test_0 test_0_4 (.in_1(alu_1_out_4), .out_2(test_0_4_out_2));
  not not_4 (not_4_out, test_0_4_out_2);
  assign or_2_out = decoder_1_adress_of_value_b | decoder_1_address_of_value_a | decoder_1_ram_address;  // OR_Gate or_2, 3 bits wide
  or or_3 (Select_code[1], decoder_1_adress_of_value_b[2], decoder_1_adress_of_value_b[1], decoder_1_adress_of_value_b[0]);
  // Probe on register_3_q
  Pull_Resistor pull_resistor_2 (.node(pull_resistor_2_node));
  Pull_Resistor pull_resistor_3 (.node(out_11));
  // Probe on register_3_q
  test_0 test_0_5 (.in_1(decoder_1_what_write), .out_2(test_0_5_out_2));
  assign or_4_out = decoder_1_what_write | alu_1_out_4;  // OR_Gate or_4, 8 bits wide
  not not_5 (not_5_out, test_0_5_out_2);
  or or_5 (or_5_out, not_5_out, not_1_out);
  Demultiplexer #(.select(2), .width(8), .enable("false")) demultiplexer_1 (
    .out1(pull_resistor_2_node), .out2(out_11), .in(Loaded_value), .sel(Select_code));  // open: out0, out3
  // Probe on register_3_q
  and and_1 (and_1_out, or_5_out, clock_2_out);
  Clock clock_2 (.out(clock_2_out));
  RAM #(.addrWidth(3), .bus("separate")) ram_1 (
    .addr(or_2_out), .din(or_4_out), .data(Loaded_value), .clk(and_1_out), .ld(1'b1),
    .clr(decoder_1_reset_ram));  // open: str, sel

  // Notes on the sheet:
  //   Program creator
  //   contents of rom_1 (hex, n*v repeats v):
  //   1200 8 2 440 10000000
endmodule

module decoder (
  input  [31:0] in_1,
  output [2:0] address_of_value_A,
  output [2:0] Adress_of_value_B,
  output [2:0] ALU_code,
  output [2:0] Ram_address,
  output [7:0] What_write,
  output Reset_ram,
  output [3:0] Jump_rom,
  output Jump_to_0
);

  wire [31:0] pull_resistor_1_node;

  Pull_Resistor pull_resistor_1 (.node(pull_resistor_1_node));
  Comparator #(.width(32)) comparator_1 (.a(in_1), .b(pull_resistor_1_node), .eq(Jump_to_0));  // open: gt, lt

  assign address_of_value_A = in_1[2:0];
  assign Adress_of_value_B = in_1[5:3];
  assign ALU_code = in_1[8:6];
  assign Jump_rom = in_1[31:28];
  assign Ram_address = in_1[11:9];
  assign Reset_ram = in_1[27];
  assign What_write = in_1[19:12];
endmodule

module delay (
  input  [2:0] in_1,
  output [2:0] out_2
);

  wire [2:0] buffer_1_out, buffer_2_out, buffer_3_out, buffer_4_out, buffer_5_out, buffer_6_out,
       buffer_7_out, buffer_8_out, buffer_9_out, buffer_10_out, buffer_11_out, buffer_12_out, buffer_13_out,
       buffer_14_out, buffer_15_out, buffer_16_out, buffer_17_out, buffer_18_out, buffer_19_out,
       buffer_20_out, buffer_21_out, buffer_22_out, buffer_23_out, buffer_24_out, buffer_25_out,
       buffer_26_out, buffer_27_out, buffer_28_out, buffer_29_out, buffer_30_out, buffer_31_out,
       buffer_32_out, buffer_33_out, buffer_34_out, buffer_35_out, buffer_36_out, buffer_37_out,
       buffer_38_out, buffer_39_out, buffer_40_out, buffer_41_out, buffer_42_out, buffer_43_out;

  assign buffer_1_out = in_1;  // Buffer buffer_1, 3 bits wide
  assign buffer_2_out = buffer_1_out;  // Buffer buffer_2, 3 bits wide
  assign buffer_3_out = buffer_4_out;  // Buffer buffer_3, 3 bits wide
  assign buffer_4_out = buffer_2_out;  // Buffer buffer_4, 3 bits wide
  assign buffer_5_out = buffer_3_out;  // Buffer buffer_5, 3 bits wide
  assign buffer_6_out = buffer_5_out;  // Buffer buffer_6, 3 bits wide
  assign buffer_7_out = buffer_8_out;  // Buffer buffer_7, 3 bits wide
  assign buffer_8_out = buffer_9_out;  // Buffer buffer_8, 3 bits wide
  assign buffer_9_out = buffer_6_out;  // Buffer buffer_9, 3 bits wide
  assign buffer_10_out = buffer_7_out;  // Buffer buffer_10, 3 bits wide
  assign buffer_11_out = buffer_10_out;  // Buffer buffer_11, 3 bits wide
  assign buffer_12_out = buffer_11_out;  // Buffer buffer_12, 3 bits wide
  assign buffer_13_out = buffer_12_out;  // Buffer buffer_13, 3 bits wide
  assign buffer_14_out = buffer_13_out;  // Buffer buffer_14, 3 bits wide
  assign buffer_15_out = buffer_17_out;  // Buffer buffer_15, 3 bits wide
  assign buffer_16_out = buffer_14_out;  // Buffer buffer_16, 3 bits wide
  assign buffer_17_out = buffer_18_out;  // Buffer buffer_17, 3 bits wide
  assign buffer_18_out = buffer_16_out;  // Buffer buffer_18, 3 bits wide
  assign buffer_19_out = buffer_15_out;  // Buffer buffer_19, 3 bits wide
  assign buffer_20_out = buffer_21_out;  // Buffer buffer_20, 3 bits wide
  assign buffer_21_out = buffer_22_out;  // Buffer buffer_21, 3 bits wide
  assign buffer_22_out = buffer_19_out;  // Buffer buffer_22, 3 bits wide
  assign buffer_23_out = buffer_24_out;  // Buffer buffer_23, 3 bits wide
  assign buffer_24_out = buffer_25_out;  // Buffer buffer_24, 3 bits wide
  assign buffer_25_out = buffer_20_out;  // Buffer buffer_25, 3 bits wide
  assign buffer_26_out = buffer_23_out;  // Buffer buffer_26, 3 bits wide
  assign buffer_27_out = buffer_28_out;  // Buffer buffer_27, 3 bits wide
  assign buffer_28_out = buffer_30_out;  // Buffer buffer_28, 3 bits wide
  assign buffer_29_out = buffer_27_out;  // Buffer buffer_29, 3 bits wide
  assign buffer_30_out = buffer_26_out;  // Buffer buffer_30, 3 bits wide
  assign buffer_31_out = buffer_34_out;  // Buffer buffer_31, 3 bits wide
  assign buffer_32_out = buffer_31_out;  // Buffer buffer_32, 3 bits wide
  assign buffer_33_out = buffer_29_out;  // Buffer buffer_33, 3 bits wide
  assign buffer_34_out = buffer_33_out;  // Buffer buffer_34, 3 bits wide
  assign buffer_35_out = buffer_32_out;  // Buffer buffer_35, 3 bits wide
  assign buffer_36_out = buffer_35_out;  // Buffer buffer_36, 3 bits wide
  assign buffer_37_out = buffer_38_out;  // Buffer buffer_37, 3 bits wide
  assign buffer_38_out = buffer_36_out;  // Buffer buffer_38, 3 bits wide
  assign buffer_39_out = buffer_40_out;  // Buffer buffer_39, 3 bits wide
  assign buffer_40_out = buffer_37_out;  // Buffer buffer_40, 3 bits wide
  assign buffer_41_out = buffer_42_out;  // Buffer buffer_41, 3 bits wide
  assign buffer_42_out = buffer_39_out;  // Buffer buffer_42, 3 bits wide
  assign buffer_43_out = buffer_41_out;  // Buffer buffer_43, 3 bits wide
  assign out_2 = buffer_43_out;  // Buffer buffer_44, 3 bits wide
endmodule

module test_0 (
  input  [7:0] in_1,
  output out_2
);

  Comparator comparator_1 (.a(in_1), .b({8{1'b0}}), .eq(out_2));  // open: gt, lt
endmodule

module coder (
  input  [2:0] address_of_value_A,
  input  [2:0] Adress_of_value_B,
  input  [2:0] ALU_code,
  input  [2:0] Ram_address,
  input  [7:0] What_write,
  input  Reset_ram,
  input  [3:0] Jump_rom,
  output [31:0] out_8
);

  Pull_Resistor pull_resistor_1 (.node({Jump_rom, Reset_ram, out_8[26:20], What_write, Ram_address, ALU_code, Adress_of_value_B, address_of_value_A}));

  assign {out_8[31:27], out_8[19:0]} = {Jump_rom, Reset_ram, What_write, Ram_address, ALU_code, Adress_of_value_B, address_of_value_A};
endmodule

module ALU (
  input  [2:0] ALU_code,
  input  [7:0] value_A,
  input  [7:0] value_B,
  output [7:0] out_4,
  output a_b,
  output a__b,
  output a_b_2,
  output Overflow_minus,
  output Overflow_plus,
  output Overflow_star
);

  wire test_0_1_out_2;
  wire [7:0] adder_1_out, divider_1_out, multiplier_1_cout, multiplier_1_out, not_2_out, or_1_out,
       subtractor_1_out, xor_1_out;

  not not_1 (Overflow_star, test_0_1_out_2);
  test_0 test_0_1 (.in_1(multiplier_1_cout), .out_2(test_0_1_out_2));
  Adder adder_1 (.a(value_A), .b(value_B), .out(adder_1_out), .cout(Overflow_plus));  // open: cin
  Subtractor subtractor_1 (.a(value_A), .b(value_B), .out(subtractor_1_out), .bout(Overflow_minus));  // open: bin
  Multiplier multiplier_1 (.a(value_A), .b(value_B), .out(multiplier_1_out), .cout(multiplier_1_cout));  // open: cin
  Divider divider_1 (.a(value_A), .b(value_B), .out(divider_1_out));  // open: upper, rem
  Comparator comparator_1 (.a(value_A), .b(value_B), .gt(a_b), .eq(a__b), .lt(a_b_2));
  assign xor_1_out = value_A ^ value_B;  // XOR_Gate xor_1, 8 bits wide
  assign or_1_out = value_A | value_B;  // OR_Gate or_1, 8 bits wide
  assign not_2_out = ~value_A;  // NOT_Gate not_2, 8 bits wide
  Multiplexer #(.select(3), .width(8), .enable("false")) multiplexer_1 (
    .in1(adder_1_out), .in2(subtractor_1_out), .in3(multiplier_1_out), .in4(divider_1_out), .in5(xor_1_out),
    .in6(or_1_out), .in7(not_2_out), .out(out_4), .sel(ALU_code));  // open: in0
endmodule

module Instruction_counter (
  input  [3:0] Jump_to,
  input  Jump_to_0,
  input  Cycles,
  input  Start,
  output [3:0] out_5
);

  wire and_1_out, not_1_out, or_1_out, or_2_out;
  wire [3:0] adder_1_out, multiplexer_1_out;

  Adder #(.width(4)) adder_1 (.a(out_5), .b(4'b0001), .out(adder_1_out));  // open: cin, cout
  not not_1 (not_1_out, Start);
  and and_1 (and_1_out, Cycles, Start);
  or or_1 (or_1_out, Jump_to[0], Jump_to[1], Jump_to[2], Jump_to[3], or_2_out);
  Multiplexer #(.width(4), .enable("false")) multiplexer_1 (
    .in0(adder_1_out), .in1(Jump_to), .out(multiplexer_1_out), .sel(or_1_out));
  or or_2 (or_2_out, Jump_to_0, not_1_out);
  Register #(.width(4)) register_1 (.D(multiplexer_1_out), .Q(out_5), .clk(and_1_out));  // open: en, clr
endmodule
