// Logisim project ptit cpu vite fait.circ as structural Verilog: 2 circuits, main circuit main
module main (
  input  in_1,
  input  [15:0] in_2,
  output [2:0] out_3
);

  wire and_1_out, clock_1_out, or_1_out;
  wire [2:0] adder_1_out, decoder_2_jump_to, multiplexer_1_out, register_1_q;
  wire [15:0] rom_1_data;

  Adder #(.width(3)) adder_1 (.a(register_1_q), .b(3'b001), .out(adder_1_out));  // open: cin, cout
  Clock clock_1 (.out(clock_1_out));
  Multiplexer #(.width(3), .enable("false")) multiplexer_1 (
    .in0(adder_1_out), .in1(decoder_2_jump_to), .out(multiplexer_1_out), .sel(or_1_out));
  and and_1 (and_1_out, clock_1_out, in_1);
  or or_1 (or_1_out, decoder_2_jump_to[2], decoder_2_jump_to[1], decoder_2_jump_to[0]);
  Register #(.width(3)) register_1 (.D(multiplexer_1_out), .Q(register_1_q), .clk(and_1_out));  // open: en, clr
  decoder decoder_1 (.in_1(in_2), .Jump_to(out_3));
  // Probe on out_3
  decoder decoder_2 (.in_1(rom_1_data), .Jump_to(decoder_2_jump_to));
  ROM #(.addrWidth(3), .dataWidth(16)) rom_1 (.addr(register_1_q), .data(rom_1_data));  // open: sel

  // Notes on the sheet:
  //   contents of rom_1 (hex, n*v repeats v):
  //   2
endmodule

module decoder (
  input  [15:0] in_1,
  output [2:0] Jump_to
);


  assign Jump_to = in_1[2:0];
endmodule
